// Logisim project problem2.circ as structural Verilog: 16 circuits, main circuit BIRD
module deneme (
);

  wire a1, a2, a3, a4, b1, b2, b3, b4, c1, c2, c3, c4, d1, d2, d3, d4, e1, e2, e3, e4, f1, f2, f3, f4, g1,
       g2, g3, g4;
  wire [15:0] out;

  _7_Segment_Display u_7_segment_display_1 (.g(g3), .f(f3), .a(a3), .b(b3), .e(e3), .d(d3), .c(c3));  // open: dp
  _7_Segment_Display u_7_segment_display_2 (.g(g4), .f(f4), .a(a4), .b(b4), .e(e4), .d(d4), .c(c4));  // open: dp
  _7_Segment_Display u_7_segment_display_3 (.g(g2), .f(f2), .a(a2), .b(b2), .e(e2), .d(d2), .c(c2));  // open: dp
  _7_Segment_Display u_7_segment_display_4 (.g(g1), .f(f1), .a(a1), .b(b1), .e(e1), .d(d1), .c(c1));  // open: dp
  bin2hex bin2hex_1 (
    .D(out[15]), .C(out[14]), .B(out[13]), .A(out[12]), .a_2(a4), .b_2(b4), .c_2(c4), .d_2(d4), .e(e4),
    .f(f4), .g(g4));
  bin2hex bin2hex_2 (
    .D(out[3]), .C(out[2]), .B(out[1]), .A(out[0]), .a_2(a1), .b_2(b1), .c_2(c1), .d_2(d1), .e(e1), .f(f1),
    .g(g1));
  bin2hex bin2hex_3 (
    .D(out[7]), .C(out[6]), .B(out[5]), .A(out[4]), .a_2(a2), .b_2(b2), .c_2(c2), .d_2(d2), .e(e2), .f(f2),
    .g(g2));
  bin2hex bin2hex_4 (
    .D(out[11]), .C(out[10]), .B(out[9]), .A(out[8]), .a_2(a3), .b_2(b3), .c_2(c3), .d_2(d3), .e(e3), .f(f3),
    .g(g3));
endmodule

module Main_Box (
  input  [15:0] _16_bit_Pin1,
  input  [15:0] _16_bit_Pin2,
  output [15:0] REG
);

  wire _900, a1, a2, a3, a4, addr0, addr11, B00, b1, b2, b3, b4, bird_1_memwt, C00, c1, c2, c3, c4, clk, d1,
       d2, d3, d4, e1, e2, e3, e4, f1, f2, f3, f4, g1, g2, g3, g4, memwt, output_load, ready1, ready2;
  wire [10:1] addr11_0;
  wire [15:0] data_out, inp1OUT, inp2OUT, memory_out, multiplexer_1_out, multiplexer_2_out, multiplexer_3_out;

  Input_Device input_device_1 (
    .switches(_16_bit_Pin1), .ready(ready1), .addr_input(addr11), .A0(addr0), .clk(clk), .out(inp1OUT));
  Clock clock_1 (.out(clk));
  and u__900 (_900, ~addr11_0[1], ~addr11_0[2], ~addr11_0[3], ~addr11_0[4], ~addr11_0[5], ~addr11_0[6], ~addr11_0[7], ~addr11_0[8], addr11_0[9], ~addr11_0[10], addr11);  // AND_Gate
  and u_B00 (B00, ~addr11_0[1], ~addr11_0[2], ~addr11_0[3], ~addr11_0[4], ~addr11_0[5], ~addr11_0[6], ~addr11_0[7], addr11_0[8], addr11_0[9], ~addr11_0[10], addr11);  // AND_Gate
  and u_C00 (C00, ~addr0, ~addr11_0[1], ~addr11_0[2], ~addr11_0[3], ~addr11_0[4], ~addr11_0[5], ~addr11_0[6], ~addr11_0[7], ~addr11_0[8], ~addr11_0[9], addr11_0[10], addr11);  // AND_Gate
  Input_Device input_device_2 (
    .switches(_16_bit_Pin2), .ready(ready2), .addr_input(addr11), .A0(addr0), .clk(clk), .out(inp2OUT));
  Multiplexer #(.width(16), .enable("false")) multiplexer_1 (
    .in0({16{1'b0}}), .in1(inp1OUT), .out(multiplexer_1_out), .sel(_900));
  Multiplexer #(.width(16), .enable("false")) multiplexer_2 (
    .in0(multiplexer_1_out), .in1(inp2OUT), .out(multiplexer_2_out), .sel(B00));
  BIRD bird_1 (
    .memwt(bird_1_memwt), .addressout({addr11, addr11_0, addr0}), .dataout(data_out),
    .datain(multiplexer_3_out), .in_2(clk));
  Multiplexer #(.width(16), .enable("false")) multiplexer_3 (
    .in0(memory_out), .in1(multiplexer_2_out), .out(multiplexer_3_out), .sel(addr11));
  RAM #(.addrWidth(12), .dataWidth(16), .bus("separate")) ram_1 (
    .addr({addr11, addr11_0, addr0}), .din(data_out), .data(memory_out), .str(memwt), .clk(clk));  // open: sel, ld, clr
  and and_1 (memwt, ~addr11, bird_1_memwt);  // AND_Gate
  and and_2 (output_load, bird_1_memwt, addr11);
  _16_bit_reg u_16_bit_reg_1 (.clk(clk), .ld(output_load), .dout(REG), .din(data_out));
  Clock clock_2 (.out(clk));
  Button button_1 (.out(ready1));
  Button button_2 (.out(ready2));
  _7_Segment_Display u_7_segment_display_1 (.g(g3), .f(f3), .a(a3), .b(b3), .e(e3), .d(d3), .c(c3));  // open: dp
  _7_Segment_Display u_7_segment_display_2 (.g(g4), .f(f4), .a(a4), .b(b4), .e(e4), .d(d4), .c(c4));  // open: dp
  _7_Segment_Display u_7_segment_display_3 (.g(g2), .f(f2), .a(a2), .b(b2), .e(e2), .d(d2), .c(c2));  // open: dp
  _7_Segment_Display u_7_segment_display_4 (.g(g1), .f(f1), .a(a1), .b(b1), .e(e1), .d(d1), .c(c1));  // open: dp
  bin2hex bin2hex_1 (
    .D(REG[15]), .C(REG[14]), .B(REG[13]), .A(REG[12]), .a_2(a4), .b_2(b4), .c_2(c4), .d_2(d4), .e(e4),
    .f(f4), .g(g4));
  bin2hex bin2hex_2 (
    .D(REG[3]), .C(REG[2]), .B(REG[1]), .A(REG[0]), .a_2(a1), .b_2(b1), .c_2(c1), .d_2(d1), .e(e1), .f(f1),
    .g(g1));
  bin2hex bin2hex_3 (
    .D(REG[7]), .C(REG[6]), .B(REG[5]), .A(REG[4]), .a_2(a2), .b_2(b2), .c_2(c2), .d_2(d2), .e(e2), .f(f2),
    .g(g2));
  bin2hex bin2hex_4 (
    .D(REG[11]), .C(REG[10]), .B(REG[9]), .A(REG[8]), .a_2(a3), .b_2(b3), .c_2(c3), .d_2(d3), .e(e3), .f(f3),
    .g(g3));

  // Other names for the same wires on the sheet: addr11_0 (some bits) = {addr11, addr0}; final_out[15:0] = REG;
  //   switch1[15:0] = _16_bit_Pin1; switch2[15:0] = _16_bit_Pin2
endmodule

// CPU
module BIRD (
  input  [15:0] datain,
  input  in_2,
  output [11:0] addressout,
  output [15:0] dataout,
  output memwt
);

  wire alu_1_zero, datamux, irld, mux, pcinc, pcld, pcmux, regld, sp_minus_minus, sp_plus_plus, zf, zfld;
  wire [1:0] armux;
  wire [2:0] dst, src1, src2;
  wire [5:0] opcode;
  wire [11:0] adder_1_out, alu2_12, IR_addr, multiplexer_2_out, PC_output, R7_12;
  wire [15:0] alu_1_aluresult, bit_extender_1_out, multiplexer_4_out, multiplexer_5_out, registerbank_1_reg0,
       registerbank_1_reg1, registerbank_1_reg2, registerbank_1_reg3, registerbank_1_reg4,
       registerbank_1_reg5, registerbank_1_reg6;
  wire [15:12] alu2_16, R7_16;

  Adder #(.width(12)) adder_1 (.a(PC_output), .b(IR_addr), .out(adder_1_out));  // open: cin, cout
  Multiplexer #(.select(2), .width(12), .enable("false")) multiplexer_1 (
    .in0(PC_output), .in1(alu2_12), .in2(R7_12), .out(addressout), .sel(armux));  // open: in3
  PC PC (.pc_load(pcld), .clock(in_2), .\output (PC_output), .increment(pcinc), .input_data(multiplexer_2_out));
  Multiplexer #(.width(12), .enable("false")) multiplexer_2 (
    .in0(adder_1_out), .in1(datain[11:0]), .out(multiplexer_2_out), .sel(pcmux));
  assign bit_extender_1_out = {{4{1'b0}}, PC_output};  // Bit_Extender bit_extender_1
  Multiplexer #(.width(16), .enable("false")) multiplexer_3 (
    .in0(multiplexer_5_out), .in1(bit_extender_1_out), .out(dataout), .sel(datamux));
  Registerbank registerbank_1 (
    .reg1(registerbank_1_reg1), .reg2(registerbank_1_reg2), .reg3(registerbank_1_reg3), .regdest(dst),
    .reg4(registerbank_1_reg4), .reg5(registerbank_1_reg5), .reg6(registerbank_1_reg6),
    .reg7({R7_16, R7_12}), .write_data(multiplexer_4_out), .Clock(in_2), .SP_plus_plus(sp_plus_plus),
    .SP_minus_minus(sp_minus_minus), .REGLD(regld), .reg0(registerbank_1_reg0));
  _1_bit_reg u_1_bit_reg_1 (.clk(in_2), .data_in(alu_1_zero), .data_out(zf), .ld(zfld));
  Multiplexer #(.width(16), .enable("false")) multiplexer_4 (
    .in0(alu_1_aluresult), .in1(datain), .out(multiplexer_4_out), .sel(mux));
  Multiplexer #(.select(3), .width(16), .enable("false")) multiplexer_5 (
    .in0(registerbank_1_reg0), .in1(registerbank_1_reg1), .in2(registerbank_1_reg2),
    .in3(registerbank_1_reg3), .in4(registerbank_1_reg4), .in5(registerbank_1_reg5),
    .in6(registerbank_1_reg6), .in7({R7_16, R7_12}), .out(multiplexer_5_out), .sel(src1));
  ALU alu_1 (
    .A(multiplexer_5_out), .B({alu2_16, alu2_12}), .AluOp(opcode), .AluResult(alu_1_aluresult),
    .Zero(alu_1_zero));
  Multiplexer #(.select(3), .width(16), .enable("false")) multiplexer_6 (
    .in0(registerbank_1_reg0), .in1(registerbank_1_reg1), .in2(registerbank_1_reg2),
    .in3(registerbank_1_reg3), .in4(registerbank_1_reg4), .in5(registerbank_1_reg5),
    .in6(registerbank_1_reg6), .in7({R7_16, R7_12}), .out({alu2_16, alu2_12}), .sel(src2));
  Control_Unit control_unit_1 (
    .opcode(datain[15:12]), .ZF(zf), .clock(in_2), .S_minus_minus(sp_minus_minus),
    .S_plus_plus(sp_plus_plus), .DATAMUX(datamux), .PCMUX(pcmux), .IRLD(irld), .MEMLD(memwt), .MUX(mux),
    .ZFLD(zfld), .REGLD(regld), .ARMUX(armux), .PCINC(pcinc), .PCLD(pcld));  // open: out_4, out_5
  Instruction_Register IR (
    .in_3(datain[11:0]), .src1(src1), .aluop(opcode), .src2(src2), .dst(dst), .addr(IR_addr), .clock(in_2),
    .load(irld));

  // Other names for the same wires on the sheet: addr0_11[11:0] = datain[11:0]; alu2_16[11:0] = alu2_12; clock = in_2;
  //   memld = memwt; R7_16[11:0] = R7_12
endmodule

module ALU (
  input  [15:0] A,
  input  [15:0] B,
  input  [5:0] AluOp,
  output [15:0] AluResult,
  output Zero
);

  wire [15:0] adder_1_out, adder_2_out, Bitwise_And_out, Bitwise_Not_out, Bitwise_Or_out, Bitwise_Xor_out,
       multiplexer_1_out, subtractor_1_out, subtractor_2_out;

  assign Bitwise_And_out = A & B;  // AND_Gate Bitwise_And, 16 bits wide
  assign Bitwise_Or_out = A | B;  // OR_Gate Bitwise_Or, 16 bits wide
  assign Bitwise_Xor_out = A ^ B;  // XOR_Gate Bitwise_Xor, 16 bits wide
  assign Bitwise_Not_out = ~B;  // NOT_Gate Bitwise_Not, 16 bits wide
  Adder #(.width(16)) adder_1 (.a(A), .b(B), .out(adder_1_out));  // open: cin, cout
  Subtractor #(.width(16)) subtractor_1 (.a(A), .b(B), .out(subtractor_1_out));  // open: bin, bout
  Adder #(.width(16)) adder_2 (.a(B), .b(16'h1), .out(adder_2_out));  // open: cin, cout
  Subtractor #(.width(16)) subtractor_2 (.a(B), .b(16'h1), .out(subtractor_2_out));  // open: bin, bout
  Multiplexer #(.select(3), .width(16)) multiplexer_1 (
    .in0(Bitwise_Not_out), .in1(B), .in2(adder_2_out), .in3(subtractor_2_out), .out(multiplexer_1_out),
    .sel({1'b0, AluOp[1:0]}));  // open: in4, in5, in6, in7, en
  Multiplexer #(.select(3), .width(16)) multiplexer_2 (
    .in0(adder_1_out), .in1(subtractor_1_out), .in2(Bitwise_And_out), .in3(Bitwise_Or_out),
    .in4(Bitwise_Xor_out), .in7(multiplexer_1_out), .out(AluResult), .sel(AluOp[5:3]));  // open: in5, in6, en
  nor nor_1 (Zero, AluResult[0], AluResult[1], AluResult[2], AluResult[3], AluResult[4], AluResult[5], AluResult[6], AluResult[7], AluResult[9], AluResult[10], AluResult[11], AluResult[12], AluResult[13], AluResult[14], AluResult[15], AluResult[8]);

  // Notes on the sheet:
  //   Adder
  //   Substractor
  //   Move
endmodule

module Control_Unit (
  input  [3:0] opcode,
  input  ZF,
  input  clock,
  output [3:0] out_4,
  output [17:0] out_5,
  output S_minus_minus,
  output S_plus_plus,
  output DATAMUX,
  output PCMUX,
  output IRLD,
  output MEMLD,
  output MUX,
  output ZFLD,
  output REGLD,
  output [1:0] ARMUX,
  output PCINC,
  output PCLD
);

  wire not_1_out, not_2_out, not_3_out;
  wire [1:1] and_1_out;
  wire [3:0] multiplexer_1_out, multiplexer_2_out;

  not not_1 (not_1_out, opcode[0]);
  and and_1 (and_1_out[1], not_1_out, not_2_out, opcode[2], not_3_out);
  not not_2 (not_2_out, opcode[1]);
  not not_3 (not_3_out, opcode[3]);
  Multiplexer #(.select(2), .width(4), .enable("false")) multiplexer_1 (
    .in0(opcode), .in1(opcode), .in2(4'b0000), .in3(4'b0101), .out(multiplexer_1_out),
    .sel({and_1_out[1], ZF}));
  Multiplexer #(.width(4), .enable("false")) multiplexer_2 (
    .in0(out_5[3:0]), .in1(multiplexer_1_out), .out(multiplexer_2_out), .sel(out_5[17]));
  _4_bit_reg u_4_bit_reg_1 (.clk(clock), .out_4(out_4), .din(multiplexer_2_out), .ld(1'b1));
  ROM #(.addrWidth(4), .dataWidth(18)) rom_1 (
    .addr(out_4), .data({out_5[17:15], ARMUX, out_5[12:11], MUX, MEMLD, IRLD, out_5[7], DATAMUX, out_5[5:0]}));  // open: sel

  assign {out_5[14:13], out_5[10:8], out_5[6]} = {ARMUX, MUX, MEMLD, IRLD, DATAMUX};
  assign PCINC = out_5[15];
  assign PCLD = out_5[16];
  assign PCMUX = out_5[7];
  assign REGLD = out_5[12];
  assign S_minus_minus = out_5[4];
  assign S_plus_plus = out_5[5];
  assign ZFLD = out_5[11];

  // Notes on the sheet:
  //   contents of rom_1 (hex, n*v repeats v):
  //   28100 9400 3400 2200 0 10000 0 1800 4210 2c 14250 2d 5400 14080
endmodule

// Register bank
module Registerbank (
  input  [2:0] regdest,
  input  [15:0] write_data,
  input  REGLD,
  input  Clock,
  input  SP_plus_plus,
  input  SP_minus_minus,
  output [15:0] reg0,
  output [15:0] reg1,
  output [15:0] reg2,
  output [15:0] reg3,
  output [15:0] reg4,
  output [15:0] reg5,
  output [15:0] reg6,
  output [15:0] reg7
);

  wire a1, a2, a3, a4, and_1_out, and_2_out, and_3_out, and_4_out, and_5_out, and_6_out, and_7_out,
       and_8_out, b1, b2, b3, b4, c1, c2, c3, c4, d1, d2, d3, d4, decoder_1_out0, decoder_1_out1,
       decoder_1_out2, decoder_1_out3, decoder_1_out4, decoder_1_out5, decoder_1_out6, decoder_1_out7, e1,
       e2, e3, e4, f1, f2, f3, f4, g1, g2, g3, g4;

  Decoder #(.select(3), .enable("false")) decoder_1 (
    .out0(decoder_1_out0), .out1(decoder_1_out1), .out2(decoder_1_out2), .out3(decoder_1_out3),
    .out4(decoder_1_out4), .out5(decoder_1_out5), .out6(decoder_1_out6), .out7(decoder_1_out7), .sel(regdest));
  and and_1 (and_1_out, decoder_1_out0, REGLD);
  and and_2 (and_2_out, decoder_1_out1, REGLD);
  and and_3 (and_3_out, decoder_1_out2, REGLD);
  and and_4 (and_4_out, decoder_1_out3, REGLD);
  and and_5 (and_5_out, decoder_1_out4, REGLD);
  and and_6 (and_6_out, decoder_1_out5, REGLD);
  and and_7 (and_7_out, decoder_1_out6, REGLD);
  and and_8 (and_8_out, decoder_1_out7, REGLD);
  _16_bit_reg_with_inc u_16_bit_reg_with_inc_1 (
    .din(write_data), .clk(Clock), .dout(reg7), .SP_plus_plus(SP_plus_plus), .SP_minus_minus(SP_minus_minus),
    .LD(and_8_out));
  _16_bit_reg u_16_bit_reg_1 (.clk(Clock), .ld(and_1_out), .dout(reg0), .din(write_data));
  _16_bit_reg u_16_bit_reg_2 (.clk(Clock), .ld(and_2_out), .dout(reg1), .din(write_data));
  _16_bit_reg u_16_bit_reg_3 (.clk(Clock), .ld(and_3_out), .dout(reg2), .din(write_data));
  _16_bit_reg u_16_bit_reg_4 (.clk(Clock), .ld(and_4_out), .dout(reg3), .din(write_data));
  _16_bit_reg u_16_bit_reg_5 (.clk(Clock), .ld(and_5_out), .dout(reg4), .din(write_data));
  _16_bit_reg u_16_bit_reg_6 (.clk(Clock), .ld(and_6_out), .dout(reg5), .din(write_data));
  _16_bit_reg u_16_bit_reg_7 (.clk(Clock), .ld(and_7_out), .dout(reg6), .din(write_data));
  bin2hex bin2hex_1 (
    .D(reg0[15]), .C(reg0[14]), .B(reg0[13]), .A(reg0[12]), .a_2(a4), .b_2(b4), .c_2(c4), .d_2(d4), .e(e4),
    .f(f4), .g(g4));
  bin2hex bin2hex_2 (
    .D(reg0[3]), .C(reg0[2]), .B(reg0[1]), .A(reg0[0]), .a_2(a1), .b_2(b1), .c_2(c1), .d_2(d1), .e(e1),
    .f(f1), .g(g1));
  bin2hex bin2hex_3 (
    .D(reg0[7]), .C(reg0[6]), .B(reg0[5]), .A(reg0[4]), .a_2(a2), .b_2(b2), .c_2(c2), .d_2(d2), .e(e2),
    .f(f2), .g(g2));
  bin2hex bin2hex_4 (
    .D(reg0[11]), .C(reg0[10]), .B(reg0[9]), .A(reg0[8]), .a_2(a3), .b_2(b3), .c_2(c3), .d_2(d3), .e(e3),
    .f(f3), .g(g3));
  _7_Segment_Display u_7_segment_display_1 (.g(g4), .f(f4), .a(a4), .b(b4), .e(e4), .d(d4), .c(c4));  // open: dp
  _7_Segment_Display u_7_segment_display_2 (.g(g2), .f(f2), .a(a2), .b(b2), .e(e2), .d(d2), .c(c2));  // open: dp
  _7_Segment_Display u_7_segment_display_3 (.g(g3), .f(f3), .a(a3), .b(b3), .e(e3), .d(d3), .c(c3));  // open: dp
  _7_Segment_Display u_7_segment_display_4 (.g(g1), .f(f1), .a(a1), .b(b1), .e(e1), .d(d1), .c(c1));  // open: dp
endmodule

module Instruction_Register (
  input  load,
  input  clock,
  input  [11:0] in_3,
  output [11:0] addr,
  output [2:0] dst,
  output [2:0] src1,
  output [2:0] src2,
  output [5:0] aluop
);

  _12_bit_reg u_12_bit_reg_1 (.din(in_3), .ld(load), .clk(clock), .dout(addr));

  assign aluop = addr[11:6];
  assign dst = addr[2:0];
  assign src1 = addr[8:6];
  assign src2 = addr[5:3];
endmodule

module PC (
  input  clock,
  input  [11:0] input_data,
  input  pc_load,
  input  increment,
  output [11:0] \output 
);

  wire or_1_out;
  wire [11:0] adder_1_out, multiplexer_1_out;

  or or_1 (or_1_out, pc_load, increment);
  _12_bit_reg u_12_bit_reg_1 (.din(multiplexer_1_out), .ld(or_1_out), .clk(clock), .dout(\output ));
  Adder #(.width(12)) adder_1 (.a(\output ), .b(12'h1), .out(adder_1_out));  // open: cin, cout
  Multiplexer #(.width(12), .enable("false")) multiplexer_1 (
    .in0(input_data), .in1(adder_1_out), .out(multiplexer_1_out), .sel(increment));
endmodule

// zf
module _1_bit_reg (
  input  clk,
  input  data_in,
  input  ld,
  output data_out
);

  wire and_1_out, and_2_out;

  and and_1 (and_1_out, data_in, ld);
  and and_2 (and_2_out, ~data_in, ld);  // AND_Gate
  S_R_Flip_Flop s_r_ff_1 (.S(and_1_out), .clk(clk), .R(and_2_out), .Q(data_out), .en(1'b1));  // open: Qn, preset, reset
endmodule

module _4_bit_reg (
  input  clk,
  input  [3:0] din,
  input  ld,
  output [3:0] out_4
);

  _1_bit_reg u_1_bit_reg_1 (.clk(clk), .data_in(din[0]), .data_out(out_4[0]), .ld(ld));
  _1_bit_reg u_1_bit_reg_2 (.clk(clk), .data_in(din[1]), .data_out(out_4[1]), .ld(ld));
  _1_bit_reg u_1_bit_reg_3 (.clk(clk), .data_in(din[2]), .data_out(out_4[2]), .ld(ld));
  _1_bit_reg u_1_bit_reg_4 (.clk(clk), .data_in(din[3]), .data_out(out_4[3]), .ld(ld));
endmodule

module _12_bit_reg (
  input  clk,
  input  ld,
  input  [11:0] din,
  output [11:0] dout
);

  _4_bit_reg u_4_bit_reg_1 (.clk(clk), .out_4(dout[3:0]), .din(din[3:0]), .ld(ld));
  _4_bit_reg u_4_bit_reg_2 (.clk(clk), .out_4(dout[7:4]), .din(din[7:4]), .ld(ld));
  _4_bit_reg u_4_bit_reg_3 (.clk(clk), .out_4(dout[11:8]), .din(din[11:8]), .ld(ld));
endmodule

module _16_bit_reg (
  input  clk,
  input  ld,
  input  [15:0] din,
  output [15:0] dout
);

  _4_bit_reg u_4_bit_reg_1 (.clk(clk), .out_4(dout[3:0]), .din(din[3:0]), .ld(ld));
  _4_bit_reg u_4_bit_reg_2 (.clk(clk), .out_4(dout[7:4]), .din(din[7:4]), .ld(ld));
  _4_bit_reg u_4_bit_reg_3 (.clk(clk), .out_4(dout[11:8]), .din(din[11:8]), .ld(ld));
  _4_bit_reg u_4_bit_reg_4 (.clk(clk), .out_4(dout[15:12]), .din(din[15:12]), .ld(ld));
endmodule

module _16_bit_reg_with_inc (
  input  clk,
  input  [15:0] din,
  input  LD,
  input  SP_plus_plus,
  input  SP_minus_minus,
  output [15:0] dout
);

  wire or_1_out, or_2_out;
  wire [3:0] data_0_3, data_4_7, data_8_11, data_12_15, multiplexer_1_out, multiplexer_2_out,
       multiplexer_3_out, multiplexer_4_out;
  wire [15:0] adder_1_out, subtractor_1_out;

  Multiplexer #(.width(4), .enable("false")) multiplexer_1 (
    .in0(din[3:0]), .in1(data_0_3), .out(multiplexer_1_out), .sel(or_1_out));
  Multiplexer #(.width(4), .enable("false")) multiplexer_2 (
    .in0(din[7:4]), .in1(data_4_7), .out(multiplexer_2_out), .sel(or_1_out));
  Multiplexer #(.width(4), .enable("false")) multiplexer_3 (
    .in0(din[11:8]), .in1(data_8_11), .out(multiplexer_3_out), .sel(or_1_out));
  Multiplexer #(.width(4), .enable("false")) multiplexer_4 (
    .in0(din[15:12]), .in1(data_12_15), .out(multiplexer_4_out), .sel(or_1_out));
  or or_1 (or_1_out, SP_plus_plus, SP_minus_minus);
  _4_bit_reg u_4_bit_reg_1 (.clk(clk), .out_4(dout[3:0]), .din(multiplexer_1_out), .ld(or_2_out));
  _4_bit_reg u_4_bit_reg_2 (.clk(clk), .out_4(dout[7:4]), .din(multiplexer_2_out), .ld(or_2_out));
  _4_bit_reg u_4_bit_reg_3 (.clk(clk), .out_4(dout[11:8]), .din(multiplexer_3_out), .ld(or_2_out));
  _4_bit_reg u_4_bit_reg_4 (.clk(clk), .out_4(dout[15:12]), .din(multiplexer_4_out), .ld(or_2_out));
  or or_2 (or_2_out, SP_plus_plus, SP_minus_minus, LD);
  Adder #(.width(16)) adder_1 (.a(dout), .b(16'h1), .out(adder_1_out));  // open: cin, cout
  Subtractor #(.width(16)) subtractor_1 (.a(dout), .b(16'h1), .out(subtractor_1_out));  // open: bin, bout
  Multiplexer #(.width(16), .enable("false")) multiplexer_5 (
    .in0(adder_1_out), .in1(subtractor_1_out), .out({data_12_15, data_8_11, data_4_7, data_0_3}),
    .sel(SP_minus_minus));
endmodule

module bin2hex (
  input  D,
  input  C,
  input  B,
  input  A,
  output a_2,
  output b_2,
  output c_2,
  output d_2,
  output e,
  output f,
  output g
);

  wire and_1_out, and_2_out, and_3_out, and_4_out, and_5_out, and_6_out, and_7_out, and_8_out, and_9_out,
       and_10_out, and_11_out, and_12_out, and_13_out, and_14_out, and_15_out, and_16_out, and_17_out,
       and_18_out, and_19_out, and_20_out, and_21_out, and_22_out, and_23_out, and_24_out, and_25_out,
       and_26_out, and_27_out, and_28_out, and_29_out, and_30_out, and_31_out, and_32_out, and_33_out,
       and_34_out, and_35_out, not_1_out, not_2_out, not_3_out, not_4_out, not_5_out, not_6_out, not_7_out,
       not_8_out, not_9_out, not_10_out, not_11_out, not_12_out, not_13_out, not_14_out, not_15_out,
       not_16_out, not_17_out, not_18_out, not_19_out, not_20_out, not_21_out, not_22_out, not_23_out,
       not_24_out, not_25_out, not_26_out, not_27_out, not_28_out, not_29_out, not_30_out, not_31_out,
       not_32_out, not_33_out, not_34_out, not_35_out, not_36_out, not_37_out, not_38_out, not_39_out,
       not_40_out, not_41_out, not_42_out;

  not not_1 (not_1_out, C);
  and and_1 (and_1_out, not_1_out, not_2_out);
  not not_2 (not_2_out, A);
  not not_3 (not_3_out, D);
  and and_2 (and_2_out, not_3_out, B);
  not not_4 (not_4_out, D);
  and and_3 (and_3_out, not_4_out, C, A);
  and and_4 (and_4_out, C, B);
  and and_5 (and_5_out, D, not_5_out, not_6_out);
  not not_5 (not_5_out, C);
  not not_6 (not_6_out, B);
  and and_6 (and_6_out, D, not_7_out);
  not not_7 (not_7_out, A);
  not not_8 (not_8_out, D);
  and and_7 (and_7_out, not_8_out, not_9_out);
  not not_9 (not_9_out, C);
  not not_10 (not_10_out, D);
  and and_8 (and_8_out, not_10_out, not_11_out, not_12_out);
  not not_11 (not_11_out, B);
  not not_12 (not_12_out, A);
  not not_13 (not_13_out, C);
  and and_9 (and_9_out, not_13_out, not_14_out);
  not not_14 (not_14_out, A);
  not not_15 (not_15_out, D);
  and and_10 (and_10_out, not_15_out, B, A);
  not not_16 (not_16_out, B);
  and and_11 (and_11_out, D, not_16_out, A);
  not not_17 (not_17_out, D);
  and and_12 (and_12_out, not_17_out, not_18_out);
  not not_18 (not_18_out, B);
  not not_19 (not_19_out, D);
  and and_13 (and_13_out, not_19_out, A);
  not not_20 (not_20_out, B);
  and and_14 (and_14_out, not_20_out, A);
  not not_21 (not_21_out, D);
  and and_15 (and_15_out, not_21_out, C);
  and and_16 (and_16_out, D, not_22_out);
  not not_22 (not_22_out, C);
  not not_23 (not_23_out, C);
  and and_17 (and_17_out, not_23_out, not_24_out);
  not not_24 (not_24_out, A);
  not not_25 (not_25_out, C);
  and and_18 (and_18_out, not_25_out, B);
  and and_19 (and_19_out, B, not_26_out);
  not not_26 (not_26_out, A);
  and and_20 (and_20_out, C, not_27_out, A);
  not not_27 (not_27_out, B);
  and and_21 (and_21_out, D, not_28_out);
  not not_28 (not_28_out, B);
  not not_29 (not_29_out, C);
  and and_22 (and_22_out, not_29_out, not_30_out);
  not not_30 (not_30_out, A);
  and and_23 (and_23_out, B, not_31_out);
  not not_31 (not_31_out, A);
  and and_24 (and_24_out, D, B);
  and and_25 (and_25_out, D, C);
  not not_32 (not_32_out, B);
  and and_26 (and_26_out, not_32_out, not_33_out);
  not not_33 (not_33_out, A);
  not not_34 (not_34_out, D);
  and and_27 (and_27_out, not_34_out, C, not_35_out);
  not not_35 (not_35_out, B);
  and and_28 (and_28_out, C, not_36_out);
  not not_36 (not_36_out, A);
  not not_37 (not_37_out, C);
  and and_29 (and_29_out, D, not_37_out, A);
  and and_30 (and_30_out, D, C, B);
  not not_38 (not_38_out, C);
  and and_31 (and_31_out, not_38_out, B);
  and and_32 (and_32_out, B, not_39_out);
  not not_39 (not_39_out, A);
  not not_40 (not_40_out, D);
  and and_33 (and_33_out, not_40_out, C, not_41_out);
  not not_41 (not_41_out, B);
  and and_34 (and_34_out, D, not_42_out);
  not not_42 (not_42_out, C);
  and and_35 (and_35_out, D, A);
  or or_1 (b_2, and_7_out, and_8_out, and_9_out, and_10_out, and_11_out);
  or or_2 (c_2, and_12_out, and_13_out, and_14_out, and_15_out, and_16_out);
  or or_3 (d_2, and_17_out, and_18_out, and_19_out, and_20_out, and_21_out);
  or or_4 (e, and_22_out, and_23_out, and_24_out, and_25_out);
  or or_5 (f, and_26_out, and_27_out, and_28_out, and_29_out, and_30_out);
  or or_6 (g, and_31_out, and_32_out, and_33_out, and_34_out, and_35_out);
  or or_7 (a_2, and_1_out, and_2_out, and_3_out, and_4_out, and_5_out, and_6_out);
endmodule

module signextend12_16 (
  input  [11:0] in_1,
  output [15:0] out_2
);


  assign out_2 = {{5{in_1[11]}}, in_1[10:0]};
endmodule

module Input_Device (
  input  clk,
  input  [15:0] switches,
  input  ready,
  input  addr_input,
  input  A0,
  output [15:0] out
);

  wire and_1_out, and_2_out, not_1_out;
  wire [0:0] s_r_ff_1_q;
  wire [15:0] n16_bit_reg_1_dout;

  not not_1 (not_1_out, s_r_ff_1_q[0]);
  and and_1 (and_1_out, not_1_out, ready);
  and and_2 (and_2_out, addr_input, s_r_ff_1_q[0]);
  S_R_Flip_Flop s_r_ff_1 (.S(and_1_out), .clk(clk), .R(and_2_out), .Q(s_r_ff_1_q[0]));  // open: Qn, preset, reset, en
  _16_bit_reg u_16_bit_reg_1 (.clk(clk), .ld(and_1_out), .dout(n16_bit_reg_1_dout), .din(switches));
  Multiplexer #(.width(16), .enable("false")) multiplexer_1 (
    .in0(n16_bit_reg_1_dout), .in1({{15{1'b0}}, s_r_ff_1_q[0]}), .out(out), .sel(A0));
endmodule
